# Fritzing sketch intervalometro (saved by Fritzing 0.8.5b)
breadboards: 1

parts:
  R1 = Resistor [tolerance=±5% resistance=400 package=THT]
  U1 = Optocoupler [package=THT]
  U2 = 2.5mm Audio Jack [package=stereojack2.5mm_stereojack2.5mm]
  Part1 = Arduino Uno (Rev3)

nets:
  N1: R1.Pin_0, U1.Pin_1
  N2: R1.Pin_1, Part1.D13/SCK
  N3: U1.Pin_3, Part1.GND
  N4: U1.Pin_4, U2.SLEEVE
  N5: U1.Pin_5, U2.LEFT
